# Fritzing sketch pi-lighting (saved by Fritzing 0.9.3b)
breadboards: 1

parts:
  Pi1 = Adafruit Pi Cobbler
  JACK1 = 2.1mm DC Barrel Jack
  JST1_(LEDs) = female pin header, 4 pins [form="♀ (female)"]
  FUSE = Resettable Fuse PTC [package=ptc]

nets:
  N1: Pi1.5V0, FUSE.2
  N2: Pi1.GND, JACK1.switch, JST1_(LEDs).pin2
  N3: Pi1.MOSI, JST1_(LEDs).pin3
  N4: Pi1.SCLK, JST1_(LEDs).pin4
  N5: JACK1.center, JST1_(LEDs).pin1, FUSE.1

custom parts:
  Adafruit Pi Cobbler: Adafruit Pi Cobbler GPIO Breakout for Raspberry Pi
  2.1mm DC Barrel Jack: 2.1mm DC Barrel Jack with Thru-Hole Connectors (breadboardable)
